# Fritzing sketch Breadboard Programmer (saved by Fritzing 0.9.1b)
breadboards: 1

parts:
  U1 = atmega168 [package=dip]
  Y1 = CRYSTAL [package=hc49u-v]
  C1 = Capacitor [package=cap-pth-small2]
  C2 = Capacitor [package=cap-pth-small2]

nets:
  N1: U1.GND#7, C1.1, C2.1
  N2: U1.XLAT1, Y1.1, C2.2
  N3: U1.XLAT2, Y1.2, C1.2
